# Fritzing sketch Servo_Sketch (saved by Fritzing 0.9.3b)
breadboards: 1

parts:
  Part1 = Arduino Uno (Rev3) - ICSP
  M1 = Dagu DGServo 9g (End View) [part_number=RS001B]
  M2 = Dagu DGServo 9g (End View) [part_number=RS001B]

nets:
  N1: Part1.D5_PWM, M2.pulse
  N2: Part1.D6_PWM, M1.pulse
  VCC: Part1.5V, M1.vcc, M2.vcc
  GND: Part1.GND, M1.gnd, M2.gnd

notes:
  Vertical Servo
  Horizontal
  Servo
